# Fritzing sketch ex_1_2_drawing (saved by Fritzing 0.9.3b)
breadboards: 1

parts:
  Part1 = Arduino Mega ADK (Rev3)
  R1 = PHOTOCELL [package=photocell-kit]
  LED1 = LEDs [package=led10mm]
  R2 = Resistor [tolerance=±5% resistance=10k package=THT]
  R3 = Resistor [tolerance=±5% resistance=220 package="1206 [SMD]"]

nets:
  N1: Part1.A0, R1.P$1, R3.Pin_1
  N2: Part1.GND, LED1.C, R3.Pin_0
  N3: Part1.5V, R1.P$2
  N4: Part1.D2_PWM, R2.Pin_1
  N5: LED1.A, R2.Pin_0
